// Logisim project JZ101.circ as structural Verilog: 7 circuits, main circuit main
module main (
);

  wire cpu_jz_101_1_load_mem;
  wire [15:0] cpu_jz_101_1_addr_out, cpu_jz_101_1_out, ram_1_data;

  CPU_JZ_101 cpu_jz_101_1 (
    .LOAD_MEM(cpu_jz_101_1_load_mem), .ADDR_OUT(cpu_jz_101_1_addr_out), .IN(ram_1_data),
    .OUT(cpu_jz_101_1_out));
  RAM #(.addrWidth(16), .dataWidth(16), .bus("separate")) ram_1 (
    .addr(cpu_jz_101_1_addr_out), .din(cpu_jz_101_1_out), .data(ram_1_data), .clk(cpu_jz_101_1_load_mem));  // open: str, sel, ld, clr
endmodule

module CPU_JZ_101 (
  input  [15:0] IN,
  output [15:0] OUT,
  output [15:0] ADDR_OUT,
  output LOAD_MEM
);

  wire DEST_ADDR, FLAGS_ALU, JMP_W_FLAGS, JUMP, LOAD_DEST, LOAD_FLAGS, LOAD_INS, LOAD_OPRAND, LOAD_PC,
       MATH_WITH_OP, PC_2, PC___1, SP, SP___1, SRC_ADDR;
  wire [3:0] DB_SELECT;
  wire [15:0] alu_1_ans, alu_1_flag_out, INS_REG_q, multiplexer_2_out, OPRAND_REG_q, PC_q,
       pc_select_1_pc_out, reges_1_dest_out, reges_1_flags_out, reges_1_sp_out, reges_1_src_out;

  Multiplexer #(.select(4), .width(16)) multiplexer_1 (
    .in0(IN), .in1(reges_1_src_out), .in2(reges_1_dest_out), .in3(reges_1_sp_out), .in4(alu_1_ans),
    .in5(OPRAND_REG_q), .in6(PC_q), .in7(INS_REG_q), .out(OUT), .sel(DB_SELECT));  // open: in8, in9, in10, in11, in12, in13, in14, in15, en
  CONTLOL contlol_1 (
    .LOAD_PC(LOAD_PC), .LOAD_MEM(LOAD_MEM), .LOAD_DEST(LOAD_DEST), .LOAD_FLAGS(LOAD_FLAGS),
    .LOAD_OPRAND(LOAD_OPRAND), .LOAD_INS(LOAD_INS), .ALU_TO_FLAG(FLAGS_ALU), .OPRAND_TO_ALU(MATH_WITH_OP),
    .PC___1_TO_ADDR(PC___1), .SP_TO_ADR(SP), .SP___1_TO_ADR(SP___1), .SRC_TO_ADR(SRC_ADDR),
    .DEST_TO_ADR(DEST_ADDR), .PC_TO_DB(JUMP), .PC_TO_DB_W_F(JMP_W_FLAGS), .INS_IN(OUT),
    .DB_SELECT(DB_SELECT), .PC___2(PC_2));
  Register #(.width(16)) INS_REG (.D(OUT), .Q(INS_REG_q), .clk(LOAD_INS));  // open: en, clr
  Register #(.width(16)) OPRAND_REG (.D(OUT), .Q(OPRAND_REG_q), .clk(LOAD_OPRAND));  // open: en, clr
  Multiplexer #(.width(16)) multiplexer_2 (
    .in0(reges_1_dest_out), .in1(OPRAND_REG_q), .out(multiplexer_2_out), .sel(MATH_WITH_OP));  // open: en
  ALU alu_1 (
    .X(reges_1_src_out), .Y(multiplexer_2_out), .INS(INS_REG_q), .FLAG_IN(reges_1_flags_out),
    .ANS(alu_1_ans), .FLAG_OUT(alu_1_flag_out));
  ADRR_SELECT adrr_select_1 (
    .PC___1(PC___1), .SRC_IN_2(SRC_ADDR), .DEST_IN_2(DEST_ADDR), .SP_IN_2(SP), .SP__1(SP___1), .PC_IN(PC_q),
    .OP_IN(OPRAND_REG_q), .SRC_IN(reges_1_src_out), .DEST_IN(reges_1_dest_out), .SP_IN(reges_1_sp_out),
    .OUT_ADDR(ADDR_OUT));
  REGES reges_1 (
    .INS_IN(INS_REG_q), .Write_DEST(LOAD_DEST), .SET_F_TO_ALU(FLAGS_ALU), .WRITE_FLAG(LOAD_FLAGS),
    .DB_IN(OUT), .FLAGS_IN(alu_1_flag_out), .FLAGS_OUT(reges_1_flags_out), .SP_OUT(reges_1_sp_out),
    .SRC_OUT(reges_1_src_out), .DEST_OUT(reges_1_dest_out));
  PC_SELECT pc_select_1 (
    .PC_IN(PC_q), .INS_IN(INS_REG_q), .FLAGS_IN(reges_1_flags_out), .JMP(JMP_W_FLAGS), .DJ(JUMP),
    .PC_2(PC_2), .DB_IN(OUT), .PC_OUT(pc_select_1_pc_out));
  Register #(.width(16)) PC (.D(pc_select_1_pc_out), .Q(PC_q), .clk(LOAD_PC));  // open: en, clr
endmodule

module REGES (
  input  [15:0] DB_IN,
  input  [15:0] INS_IN,
  input  Write_DEST,
  input  SET_F_TO_ALU,
  input  WRITE_FLAG,
  input  [15:0] FLAGS_IN,
  output [15:0] SRC_OUT,
  output [15:0] DEST_OUT,
  output [15:0] FLAGS_OUT,
  output [15:0] SP_OUT
);

  wire and_1_out, and_2_out, and_3_out, and_4_out, and_5_out, and_6_out, and_7_out, and_8_out, and_9_out,
       and_10_out, and_11_out, and_12_out, and_13_out, and_14_out, and_15_out, and_16_out, decoder_1_out0,
       decoder_1_out1, decoder_1_out2, decoder_1_out3, decoder_2_out0, decoder_2_out1, decoder_2_out2,
       decoder_2_out3, or_1_out;
  wire [15:0] multiplexer_1_out, register_1_q, register_2_q, register_3_q, register_4_q, register_5_q,
       register_6_q, register_7_q, register_8_q, register_9_q, register_10_q, register_12_q, register_13_q,
       register_14_q;

  Decoder #(.select(2)) decoder_1 (
    .out0(decoder_1_out0), .out1(decoder_1_out1), .out2(decoder_1_out2), .out3(decoder_1_out3),
    .sel(INS_IN[3:2]));  // open: en
  and and_1 (and_1_out, decoder_2_out0, decoder_1_out1);
  and and_2 (and_2_out, decoder_2_out0, decoder_1_out2);
  and and_3 (and_3_out, decoder_2_out0, decoder_1_out3);
  Register #(.width(16)) register_1 (.D(DB_IN), .en(and_1_out), .Q(register_1_q), .clk(Write_DEST));  // open: clr
  Register #(.width(16)) register_2 (.D(DB_IN), .en(and_2_out), .Q(register_2_q), .clk(Write_DEST));  // open: clr
  Register #(.width(16)) register_3 (.D(DB_IN), .en(and_3_out), .Q(register_3_q), .clk(Write_DEST));  // open: clr
  Decoder #(.select(2)) decoder_2 (
    .out0(decoder_2_out0), .out1(decoder_2_out1), .out2(decoder_2_out2), .out3(decoder_2_out3),
    .sel(INS_IN[1:0]));  // open: en
  and and_4 (and_4_out, decoder_2_out1, decoder_1_out0);
  and and_5 (and_5_out, decoder_2_out1, decoder_1_out1);
  and and_6 (and_6_out, decoder_2_out1, decoder_1_out2);
  and and_7 (and_7_out, decoder_2_out1, decoder_1_out3);
  Register #(.width(16)) register_4 (.D(DB_IN), .en(and_4_out), .Q(register_4_q), .clk(Write_DEST));  // open: clr
  and and_8 (and_8_out, decoder_2_out2, decoder_1_out0);
  Register #(.width(16)) register_5 (.D(DB_IN), .en(and_5_out), .Q(register_5_q), .clk(Write_DEST));  // open: clr
  and and_9 (and_9_out, decoder_2_out2, decoder_1_out1);
  Register #(.width(16)) register_6 (.D(DB_IN), .en(and_6_out), .Q(register_6_q), .clk(Write_DEST));  // open: clr
  and and_10 (and_10_out, decoder_2_out2, decoder_1_out2);
  Register #(.width(16)) register_7 (.D(DB_IN), .en(and_7_out), .Q(register_7_q), .clk(Write_DEST));  // open: clr
  and and_11 (and_11_out, decoder_2_out2, decoder_1_out3);
  Register #(.width(16)) register_8 (.D(DB_IN), .en(and_8_out), .Q(register_8_q), .clk(Write_DEST));  // open: clr
  Register #(.width(16)) register_9 (.D(DB_IN), .en(and_9_out), .Q(register_9_q), .clk(Write_DEST));  // open: clr
  Register #(.width(16)) register_10 (.D(DB_IN), .en(and_10_out), .Q(register_10_q), .clk(Write_DEST));  // open: clr
  Register #(.width(16)) register_11 (.D(DB_IN), .en(and_11_out), .Q(SP_OUT), .clk(Write_DEST));  // open: clr
  and and_12 (and_12_out, decoder_2_out3, decoder_1_out3);
  and and_13 (and_13_out, and_12_out, Write_DEST);
  Multiplexer #(.width(16)) multiplexer_1 (
    .in0(DB_IN), .in1(FLAGS_IN), .out(multiplexer_1_out), .sel(SET_F_TO_ALU));  // open: en
  and and_14 (and_14_out, decoder_2_out3, decoder_1_out0);
  and and_15 (and_15_out, decoder_2_out3, decoder_1_out1);
  and and_16 (and_16_out, decoder_2_out3, decoder_1_out2);
  or or_1 (or_1_out, and_13_out, WRITE_FLAG);
  Register #(.width(16)) register_12 (.D(DB_IN), .en(and_14_out), .Q(register_12_q), .clk(Write_DEST));  // open: clr
  Register #(.width(16)) register_13 (.D(DB_IN), .en(and_15_out), .Q(register_13_q), .clk(Write_DEST));  // open: clr
  Register #(.width(16)) register_14 (.D(DB_IN), .en(and_16_out), .Q(register_14_q), .clk(Write_DEST));  // open: clr
  Register #(.width(16)) register_15 (.D(multiplexer_1_out), .Q(FLAGS_OUT), .clk(or_1_out));  // open: en, clr
  Multiplexer #(.select(4), .width(16)) multiplexer_2 (
    .in0({16{1'b0}}), .in1(register_4_q), .in2(register_8_q), .in3(register_12_q), .in4(register_1_q),
    .in5(register_5_q), .in6(register_9_q), .in7(register_13_q), .in8(register_2_q), .in9(register_6_q),
    .in10(register_10_q), .in11(register_14_q), .in12(register_3_q), .in13(register_7_q), .in14(SP_OUT),
    .in15(FLAGS_OUT), .out(SRC_OUT), .sel(INS_IN[7:4]));  // open: en
  Multiplexer #(.select(4), .width(16)) multiplexer_3 (
    .in0({16{1'b0}}), .in1(register_4_q), .in2(register_8_q), .in3(register_12_q), .in4(register_1_q),
    .in5(register_5_q), .in6(register_9_q), .in7(register_13_q), .in8(register_2_q), .in9(register_6_q),
    .in10(register_10_q), .in11(register_14_q), .in12(register_3_q), .in13(register_7_q), .in14(SP_OUT),
    .in15(FLAGS_OUT), .out(DEST_OUT), .sel(INS_IN[3:0]));  // open: en
endmodule

module ADRR_SELECT (
  input  [15:0] PC_IN,
  input  [15:0] OP_IN,
  input  [15:0] SRC_IN,
  input  [15:0] DEST_IN,
  input  [15:0] SP_IN,
  input  PC___1,
  input  SRC_IN_2,
  input  DEST_IN_2,
  input  SP_IN_2,
  input  SP__1,
  output [15:0] OUT_ADDR
);

  wire or_1_out, or_2_out;
  wire [1:0] or_3_out;
  wire [15:0] adder_1_out, adder_2_out, multiplexer_1_out, multiplexer_2_out, multiplexer_3_out,
       subtractor_1_out, subtractor_2_out;

  or or_1 (or_1_out, SP_IN_2, SP__1);
  Subtractor #(.width(16)) subtractor_1 (.a(SP_IN), .b(16'h1), .out(subtractor_1_out));  // open: bin, bout
  or or_2 (or_2_out, SRC_IN_2, DEST_IN_2);
  Multiplexer #(.width(16)) multiplexer_1 (
    .in0(SP_IN), .in1(subtractor_1_out), .out(multiplexer_1_out), .sel(SP__1));  // open: en
  Multiplexer #(.width(16)) multiplexer_2 (
    .in0(SRC_IN), .in1(DEST_IN), .out(multiplexer_2_out), .sel(DEST_IN_2));  // open: en
  or or_3 (or_3_out[0], PC___1, or_1_out);
  or or_4 (or_3_out[1], or_2_out, or_1_out);
  Adder #(.width(16)) adder_1 (.a(PC_IN), .b(16'h1), .out(adder_1_out));  // open: cin, cout
  Adder #(.width(16)) adder_2 (.a(multiplexer_2_out), .b({1'b0, OP_IN[14:0]}), .out(adder_2_out));  // open: cin, cout
  Subtractor #(.width(16)) subtractor_2 (
    .a(multiplexer_2_out), .b({1'b0, OP_IN[14:0]}), .out(subtractor_2_out));  // open: bin, bout
  Multiplexer #(.width(16)) multiplexer_3 (
    .in0(adder_2_out), .in1(subtractor_2_out), .out(multiplexer_3_out), .sel(OP_IN[15]));  // open: en
  Multiplexer #(.select(2), .width(16)) multiplexer_4 (
    .in0(PC_IN), .in1(adder_1_out), .in2(multiplexer_3_out), .in3(multiplexer_1_out), .out(OUT_ADDR),
    .sel(or_3_out));  // open: en
endmodule

module PC_SELECT (
  input  [15:0] DB_IN,
  input  [15:0] PC_IN,
  input  [15:0] INS_IN,
  input  [15:0] FLAGS_IN,
  input  JMP,
  input  DJ,
  input  PC_2,
  output [15:0] PC_OUT
);

  wire and_1_out, multiplexer_2_out, or_1_out;
  wire [15:0] adder_1_out, multiplexer_1_out;

  Multiplexer #(.width(16)) multiplexer_1 (.in0(16'h1), .in1(16'h2), .out(multiplexer_1_out), .en(PC_2));  // open: sel
  or or_1 (or_1_out, DJ, and_1_out);
  and and_1 (and_1_out, JMP, multiplexer_2_out);
  Adder #(.width(16)) adder_1 (.a(PC_IN), .b(multiplexer_1_out), .out(adder_1_out));  // open: cin, cout
  Multiplexer #(.select(4)) multiplexer_2 (
    .in0(FLAGS_IN[0]), .in1(FLAGS_IN[1]), .in2(FLAGS_IN[2]), .in3(FLAGS_IN[3]), .in4(FLAGS_IN[4]),
    .in5(FLAGS_IN[5]), .in6(1'b1), .out(multiplexer_2_out), .sel(INS_IN[11:8]));  // open: in7, in8, in9, in10, in11, in12, in13, in14, in15, en
  Multiplexer #(.width(16)) multiplexer_3 (.in0(adder_1_out), .in1(DB_IN), .out(PC_OUT), .en(or_1_out));  // open: sel
endmodule

module ALU (
  input  [15:0] X,
  input  [15:0] Y,
  input  [15:0] INS,
  input  [15:0] FLAG_IN,
  output [15:0] ANS,
  output [15:0] FLAG_OUT
);

  wire adder_1_cout, decoder_1_out9, decoder_1_out10, decoder_1_out11, decoder_1_out12, decoder_1_out15,
       or_1_out, subtractor_1_bout;
  wire [1:0] comparator_2_eq;
  wire [4:2] comparator_1_gt;
  wire [15:0] adder_1_out, and_2_out, or_2_out, subtractor_1_out, xor_1_out;
  wire [15:15] and_1_out;

  Decoder #(.select(4)) decoder_1 (
    .out9(decoder_1_out9), .out10(decoder_1_out10), .out11(decoder_1_out11), .out12(decoder_1_out12),
    .out15(decoder_1_out15), .sel(INS[11:8]));  // open: out0, out1, out2, out3, out4, out5, out6, out7, out8, out13, out14, en
  or or_1 (or_1_out, decoder_1_out9, decoder_1_out10, decoder_1_out11, decoder_1_out12);
  and and_1 (and_1_out[15], or_1_out, FLAG_IN[1]);
  Adder #(.width(16)) adder_1 (.a(X), .b(Y), .out(adder_1_out), .cin(and_1_out[15]), .cout(adder_1_cout));
  Subtractor #(.width(16)) subtractor_1 (
    .a(X), .b(Y), .out(subtractor_1_out), .bin(and_1_out[15]), .bout(subtractor_1_bout));
  assign and_2_out = X;  // AND_Gate and_2, 16 bits wide AND_Gate
  assign or_2_out = X;  // OR_Gate or_2, 16 bits wide OR_Gate
  assign xor_1_out = X ^ Y;  // XOR_Gate xor_1, 16 bits wide
  Comparator #(.width(16), .mode("unsigned")) comparator_1 (
    .a(Y), .b(X), .gt(comparator_1_gt[2]), .eq(comparator_1_gt[3]), .lt(comparator_1_gt[4]));
  Multiplexer #(.width(16)) multiplexer_1 (
    .in0({FLAG_IN[15:2], comparator_2_eq}), .in1({{11{1'b0}}, comparator_1_gt, FLAG_IN[1:0]}),
    .out(FLAG_OUT), .sel(decoder_1_out15));  // open: en
  Multiplexer #(.select(4)) multiplexer_2 (
    .in0(adder_1_cout), .in1(subtractor_1_bout), .in2(X[15]), .in3(X[0]), .in4(FLAG_IN[1]), .in5(FLAG_IN[1]),
    .in6(FLAG_IN[1]), .in7(adder_1_cout), .in8(subtractor_1_bout), .in9(adder_1_cout),
    .in10(subtractor_1_bout), .in11(X[15]), .in12(X[0]), .in13(FLAG_IN[1]), .in14(FLAG_IN[1]),
    .in15(FLAG_IN[1]), .out(comparator_2_eq[1]), .sel(INS[11:8]));  // open: en
  Multiplexer #(.select(4), .width(16)) multiplexer_3 (
    .in0(adder_1_out), .in1(subtractor_1_out), .in2({X[14:0], and_1_out[15]}),
    .in3({and_1_out[15], X[15:1]}), .in4(and_2_out), .in5(or_2_out), .in6(xor_1_out), .in7(adder_1_out),
    .in8(subtractor_1_out), .in9(adder_1_out), .in10(subtractor_1_out), .in11({and_1_out[15], X[15:1]}),
    .in12(and_2_out), .in13(Y), .in14(Y), .in15(Y), .out(ANS), .sel(INS[11:8]));  // open: en
  Comparator #(.width(16), .mode("unsigned")) comparator_2 (
    .a(ANS), .b({16{1'b0}}), .eq(comparator_2_eq[0]));  // open: gt, lt
endmodule

module CONTLOL (
  input  [15:0] INS_IN,
  output LOAD_PC,
  output LOAD_MEM,
  output LOAD_DEST,
  output LOAD_FLAGS,
  output LOAD_OPRAND,
  output LOAD_INS,
  output ALU_TO_FLAG,
  output OPRAND_TO_ALU,
  output PC___1_TO_ADDR,
  output SP_TO_ADR,
  output SP___1_TO_ADR,
  output SRC_TO_ADR,
  output DEST_TO_ADR,
  output PC_TO_DB,
  output PC_TO_DB_W_F,
  output PC___2,
  output [3:0] DB_SELECT
);

  wire clock_1_out, decoder_1_out15, decoder_2_out1, decoder_2_out2, decoder_2_out7, decoder_2_out8, or_1_out;
  wire [5:0] or_2_out;
  wire [7:0] adder_1_out, multiplexer_1_out, register_1_q, rom_1_data;
  wire [11:0] rom_2_data;

  Clock clock_1 (.out(clock_1_out));
  or or_1 (or_1_out, clock_1_out, decoder_1_out15);
  ROM rom_1 (.addr(INS_IN[15:8]), .data(rom_1_data));  // open: sel
  Multiplexer #(.width(8)) multiplexer_1 (
    .in0(adder_1_out), .in1(rom_1_data), .out(multiplexer_1_out), .sel(or_2_out[5]));  // open: en
  Register register_1 (.D(multiplexer_1_out), .Q(register_1_q), .clk(or_1_out));  // open: en, clr
  Adder adder_1 (.a(register_1_q), .b(8'h1), .out(adder_1_out));  // open: cin, cout
  ROM #(.dataWidth(12)) rom_2 (
    .addr(register_1_q), .data({rom_2_data[11:8], DB_SELECT, rom_2_data[3:0]}));  // open: sel
  Decoder #(.select(4)) decoder_1 (
    .out1(or_2_out[5]), .out2(PC___1_TO_ADDR), .out4(OPRAND_TO_ALU), .out5(SRC_TO_ADR), .out6(DEST_TO_ADR),
    .out7(SP_TO_ADR), .out8(SP___1_TO_ADR), .out15(decoder_1_out15), .sel(rom_2_data[11:8]));  // open: out0, out3, out9, out10, out11, out12, out13, out14, en
  Decoder #(.select(4)) decoder_2 (
    .out1(decoder_2_out1), .out2(decoder_2_out2), .out3(PC_TO_DB_W_F), .out4(PC_TO_DB), .out5(PC___2),
    .out7(decoder_2_out7), .out8(decoder_2_out8), .out9(ALU_TO_FLAG), .sel(rom_2_data[3:0]));  // open: out0, out6, out10, out11, out12, out13, out14, out15, en
  or or_2 (or_2_out[0], decoder_2_out1, PC_TO_DB_W_F, PC_TO_DB, decoder_2_out7, decoder_2_out8, ALU_TO_FLAG);
  or or_3 (or_2_out[1], decoder_2_out1, decoder_2_out2);
  or or_4 (or_2_out[2], decoder_2_out8, ALU_TO_FLAG);
  Multiplexer #(.width(6)) multiplexer_2 (
    .in0({or_2_out[5], PC___1_TO_ADDR, ALU_TO_FLAG, or_2_out[2:0]}), .in1({6{1'b0}}),
    .out({LOAD_INS, LOAD_OPRAND, LOAD_FLAGS, LOAD_DEST, LOAD_MEM, LOAD_PC}), .sel(or_1_out));  // open: en

  // Notes on the sheet:
  //   contents of rom_1 (hex, n*v repeats v):
  //   48*0 7*9 b b 7*9 5*11 e 15*0 14 15*0 19 58*0 3 15*0 5 15*0 7 62*0 ff
  //   contents of rom_2 (hex, n*v repeats v):
  //   0 7 100 508 100 611 100 18 100 49 100 200 449 100 200 54 100 200 53 100 200 7 762 55 100 704 100
  //   228*0 f00
endmodule
